# Fritzing sketch flashlight (saved by Fritzing 0.9.3b)
breadboards: 1

parts:
  Part1 = Arduino Nano (Rev3.0)
  S1 = Pushbutton [package="[THT]"]
  R1 = Resistor [tolerance=±10% resistance=1k package=THT]
  R2 = Resistor [tolerance=±5% resistance=47 package="2512 [SMD]"]
  LED1 = LED - 5mm [color="Infrared (940nm)" package="5 mm [THT]"]
  LED2 = LED - 5mm [color="White (4500K)" package="5 mm [THT]"]
  LED3 = smd LED [color="Blue (525nm)" package="0805 [SMD]"]

nets:
  N1: Part1.GND, R1.Pin_1, LED1.cathode, LED2.cathode, LED3.cathode
  N2: Part1.D2, S1.Pin_1, S1.Pin_2, R1.Pin_0
  N3: Part1.D3, LED3.anode
  N4: Part1.D4, LED2.anode
  N5: Part1.D5, R2.Pin_1
  N6: Part1.3V3, S1.Pin_3, S1.Pin_4
  N7: R2.Pin_0, LED1.anode
