# Fritzing sketch lock_box (saved by Fritzing 0.9.3b)
breadboards: 1

parts:
  Part1 = Arduino Nano (Rev3.0)
  L1 = Solenoid
  Q1 = Basic FET N-Channel [package="D2Pak [SMD]"]
  S3 = Pushbutton [package="[THT]"]
  R1 = Resistor [tolerance=±10% resistance=1k package="1206 [SMD]"]
  VCC1 = Battery block 9V
  D1 = P1000K [part_number=P1000K]

nets:
  N1: Part1.GND, Q1.source, R1.Pin_1, VCC1.-
  N2: Part1.5V, S3.Pin_3, S3.Pin_4
  N3: L1.pin1, Q1.drain, D1.anode
  N4: Q1.Gate, S3.Pin_1, S3.Pin_2, R1.Pin_0
  N5: VCC1.+, D1.cathode
