# Fritzing sketch gates (saved by Fritzing 0.9.3b)
breadboards: 1

parts:
  Part1 = Arduino Nano (Rev3.0) (ICSP)
  S1 = Momentary Switch [package=ksa_sealed_tac_switch]
  S2 = Momentary Switch [package=ksa_sealed_tac_switch]
  LED1 = smd LED [color="Yellow (595nm)" package="0805 [SMD]"]
  LED2 = smd LED [color="Green (555nm)" package="0805 [SMD]"]
  R1 = Resistor [tolerance=±5% resistance=220 package="0402 [SMD]"]
  R2 = Resistor [tolerance=±5% resistance=220 package="0402 [SMD]"]
  R3 = Resistor [tolerance=±5% resistance=220 package="0402 [SMD]"]
  R4 = Resistor [tolerance=±5% resistance=220 package="0402 [SMD]"]
  R5 = Resistor [tolerance=±5% resistance=220 package="0402 [SMD]"]
  LED3 = smd LED [color="Red (633nm)" package="0805 [SMD]"]

nets:
  N1: Part1.GND, R1.Pin_0, R2.Pin_0, R3.Pin_1, R4.Pin_1, R5.Pin_0
  N2: Part1.D3, S2.2, R5.Pin_1
  N3: Part1.D4, S1.2, R1.Pin_1
  N4: Part1.D6, LED1.cathode
  N5: Part1.D7, LED3.cathode
  N6: Part1.D10, LED2.cathode
  N7: Part1.5V, S1.4, S2.4
  N8: LED1.anode, R3.Pin_0
  N9: LED2.anode, R4.Pin_0
  N10: R2.Pin_1, LED3.anode
