# Fritzing sketch MothMobile (saved by Fritzing 0.9.3b)
breadboards: 1

parts:
  Part1 = Arduino Nano (Rev3.0)
  J1 = Basic Servo
  J2 = Basic Servo
  R1 = Resistor [tolerance=±5% resistance=220 package="2512 [SMD]"]
  R2 = Resistor [tolerance=±5% resistance=220 package="2512 [SMD]"]
  R3 = Resistor [tolerance=±5% resistance=220 package="2512 [SMD]"]
  R4 = Resistor [tolerance=±5% resistance=220 package="2512 [SMD]"]
  R5 = Photocell (LDR) [package=THT]
  R6 = PHOTOCELL [package=photocell-kit]
  R8 = PHOTOCELL [package=photocell-kit]
  R9 = PHOTOCELL [package=photocell-kit]

nets:
  GND: Part1.GND, J1.gnd, J2.gnd, R1.Pin_0, R2.Pin_0, R3.Pin_0, R4.Pin_0
  N1: Part1.D5, J1.pulse
  N2: Part1.D6, J2.pulse
  VCC: Part1.5V, J1.vcc, J2.vcc, R5.pin_0, R5.pin_1, R6.P$1, R8.P$2, R9.P$1
  N3: Part1.A3, R3.Pin_1, R9.P$2
  N4: Part1.A2, R1.Pin_1, R8.P$1
  N5: Part1.A1, R2.Pin_1, R6.P$2
  N6: Part1.A0, R4.Pin_1
