# Fritzing sketch saw (saved by Fritzing 0.9.3b)
breadboards: 1

parts:
  Part1 = Arduino Nano (Rev3.0)
  R1 = Rotary Potentiometer (Small) [maximum_resistance=100kΩ package=THT]
  J1 = Basic Servo
  S1 = Pushbutton [package="[THT]"]

nets:
  GND: Part1.GND, R1.leg1, J1.gnd
  N1: Part1.5V, R1.leg2, S1.Pin_4
  N2: Part1.A1, R1.wiper
  N3: Part1.A0, J1.pulse
  N4: J1.vcc, S1.Pin_1, S1.Pin_2
