# Fritzing sketch bitCircuit (saved by Fritzing 0.9.3b)
breadboards: 1

parts:
  Part1 = Arduino Nano (Rev3.0)
  LED5 = smd LED [color="Red (633nm)" package="0805 [SMD]"]
  LED6 = smd LED [color="Red (633nm)" package="0805 [SMD]"]
  LED7 = smd LED [color="Red (633nm)" package="0805 [SMD]"]
  LED8 = smd LED [color="Red (633nm)" package="0805 [SMD]"]
  R1 = Resistor [tolerance=±5% resistance=220 package="2010 [SMD]"]

nets:
  N1: Part1.GND, R1.Pin_0
  N2: Part1.D2, LED5.anode
  N3: Part1.D3, LED6.anode
  N4: Part1.D4, LED7.anode
  N5: Part1.D5, LED8.anode
  N6: LED5.cathode, LED6.cathode, LED7.cathode, LED8.cathode, R1.Pin_1
